// Logisim project Vrata_Version0.2.0.circ as structural Verilog: 18 circuits, main circuit main
module main (
);

  wire _0_out, _1, _1_out, _2, _2_out, _3, _3_out, _4, _4_out, _5, _5_out, _6, _6_out, _7, _7_out, _8,
       _8_out, _9, _9_out, _10, _15, _16, _17, _18, _24, _26, C_out, OK_out;
  wire [2:0] kod_1__1__cifra, kod_1__1__cifra_2, kod_1__1__cifra_3, kod_1__2__cifra, kod_1__2__cifra_2,
       kod_1__2__cifra_3, kod_1__3__cifra, kod_1__3__cifra_2, kod_1__3__cifra_3, kod_1__4__cifra,
       kod_1__4__cifra_2, kod_1__4__cifra_3, kod_1_out_17, kod_1_out_18, kod_1_out_19;
  wire [3:0] _11, _12, _13, _14, _25;
  wire [7:0] _27, _28, _29, _30, _31, _32, _33, _34, _35, _36, _37, _38, _39, _40, _41, _42,
       cabelmanagment_1_out_9, cabelmanagment_1_out_10, cabelmanagment_1_out_11, cabelmanagment_1_out_12,
       cabelmanagment_1_out_13, cabelmanagment_1_out_14, cabelmanagment_1_out_15, cabelmanagment_1_out_16,
       cabelmanagment_2_out_9, cabelmanagment_2_out_10, cabelmanagment_2_out_11, cabelmanagment_2_out_12,
       cabelmanagment_2_out_13, cabelmanagment_2_out_14, cabelmanagment_2_out_15, cabelmanagment_2_out_16,
       matrixauta_1_out_3, matrixauta_1_out_4, matrixauta_1_out_5, matrixauta_1_out_6, matrixauta_1_out_7,
       matrixauta_1_out_8, matrixauta_1_out_9, matrixauta_1_out_10, matrixauta_1_out_11, matrixauta_1_out_12,
       matrixauta_1_out_13, matrixauta_1_out_14, matrixauta_1_out_15, matrixauta_1_out_16,
       matrixauta_1_out_17, matrixauta_1_out_18, matrixauta_1_out_19, matrixauta_1_out_20,
       matrixauta_1_out_21, matrixauta_1_out_22, matrixauta_1_out_23, matrixauta_1_out_24,
       matrixauta_1_out_25, matrixauta_1_out_26, matrixauta_1_out_27, matrixauta_1_out_28,
       matrixauta_1_out_29, matrixauta_1_out_30;
  wire [31:0] \stavbranydisplay_1__1__řádek , \stavbranydisplay_1__2__řádek , \stavbranydisplay_1__3__řádek ,
       \stavbranydisplay_1__4__řádek , \stavbranydisplay_1__5__řádek ;

  Hex_Digit_Display hex_digit_display_1 (.value(_14));  // open: dp
  Hex_Digit_Display hex_digit_display_2 (.value(_25));  // open: dp
  Button S (.out(_15));
  MatrixAuta matrixauta_1 (
    .out_3(matrixauta_1_out_3), .out_6(matrixauta_1_out_6), .out_9(matrixauta_1_out_9),
    .out_11(matrixauta_1_out_11), .out_13(matrixauta_1_out_13), .out_15(matrixauta_1_out_15),
    .out_17(matrixauta_1_out_17), .out_19(matrixauta_1_out_19), .out_21(matrixauta_1_out_21),
    .out_23(matrixauta_1_out_23), .out_25(matrixauta_1_out_25), .out_27(matrixauta_1_out_27),
    .out_29(matrixauta_1_out_29), .out_4(matrixauta_1_out_4), .out_7(matrixauta_1_out_7),
    .out_10(matrixauta_1_out_10), .out_12(matrixauta_1_out_12), .out_14(matrixauta_1_out_14),
    .out_16(matrixauta_1_out_16), .out_18(matrixauta_1_out_18), .out_20(matrixauta_1_out_20),
    .out_22(matrixauta_1_out_22), .out_24(matrixauta_1_out_24), .out_26(matrixauta_1_out_26),
    .out_28(matrixauta_1_out_28), .out_30(matrixauta_1_out_30), .in_1(_18), .in_2(_16),
    .out_5(matrixauta_1_out_5), .out_8(matrixauta_1_out_8));
  Hex_Digit_Display hex_digit_display_3 (.value(_13));  // open: dp
  DotMatrix #(.matrixcols(13), .matrixrows(8)) dotmatrix_1 (
    .col0(matrixauta_1_out_3), .col1(matrixauta_1_out_6), .col2(matrixauta_1_out_9),
    .col3(matrixauta_1_out_11), .col4(matrixauta_1_out_13), .col5(matrixauta_1_out_15),
    .col6(matrixauta_1_out_17), .col7(matrixauta_1_out_19), .col8(matrixauta_1_out_21),
    .col9(matrixauta_1_out_23), .col10(matrixauta_1_out_25), .col11(matrixauta_1_out_27),
    .col12(matrixauta_1_out_29));
  kod kod_1 (
    ._7(_7_out), ._8(_8_out), ._9(_9_out), ._4(_4_out), ._5(_5_out), ._6(_6_out), ._1(_1_out), ._2(_2_out),
    ._3(_3_out), .C(C_out), ._0(_0_out), .OK(OK_out), .\Odemknuto_Zamčeno (_17), .Zavreno(_10),
    .out_17(kod_1_out_17), .out_18(kod_1_out_18), .out_19(kod_1_out_19), ._1__Cifra(kod_1__1__cifra),
    ._1__Cifra_2(kod_1__1__cifra_2), ._1__Cifra_3(kod_1__1__cifra_3), ._2__Cifra(kod_1__2__cifra),
    ._2__Cifra_2(kod_1__2__cifra_2), ._2__Cifra_3(kod_1__2__cifra_3), ._3__Cifra(kod_1__3__cifra),
    ._3__Cifra_2(kod_1__3__cifra_2), ._3__Cifra_3(kod_1__3__cifra_3), ._4__Cifra(kod_1__4__cifra),
    ._4__Cifra_2(kod_1__4__cifra_2), ._4__Cifra_3(kod_1__4__cifra_3), .out_15(_25), .Force_reset(_26));
  Button C (.out(C_out));
  LED led_1 (.in(_5));
  LED led_2 (.in(_4));
  stavbranydisplay stavbranydisplay_1 (
    .\_1__Řádek (\stavbranydisplay_1__1__řádek ), .\_2__Řádek (\stavbranydisplay_1__2__řádek ),
    .\_3__Řádek (\stavbranydisplay_1__3__řádek ), .\_4__Řádek (\stavbranydisplay_1__4__řádek ),
    .\_5__Řádek (\stavbranydisplay_1__5__řádek ), .\Otevřeno (_8), .\Zavřeno (_10), .\Otevírání (_7),
    .\Zavírání (_9));
  DotMatrix #(.inputtype("row"), .matrixcols(32), .matrixrows(5)) dotmatrix_2 (
    .row0(\stavbranydisplay_1__1__řádek ), .row1(\stavbranydisplay_1__2__řádek ),
    .row2(\stavbranydisplay_1__3__řádek ), .row3(\stavbranydisplay_1__4__řádek ),
    .row4(\stavbranydisplay_1__5__řádek ));
  DotMatrix #(.matrixcols(1), .matrixrows(3)) dotmatrix_3 ();  // open: col0
  DotMatrix #(.matrixcols(3), .matrixrows(3)) dotmatrix_4 (
    .col0(kod_1__1__cifra), .col1(kod_1__1__cifra_2), .col2(kod_1__1__cifra_3));
  Button u__1 (.out(_1_out));
  Button _0 (.out(_0_out));
  Button u__2 (.out(_2_out));
  Button OK (.out(OK_out));
  LED led_3 (.in(_6));
  DotMatrix #(.matrixcols(13), .matrixrows(8)) dotmatrix_5 (
    .col0(matrixauta_1_out_4), .col1(matrixauta_1_out_7), .col2(matrixauta_1_out_10),
    .col3(matrixauta_1_out_12), .col4(matrixauta_1_out_14), .col5(matrixauta_1_out_16),
    .col6(matrixauta_1_out_18), .col7(matrixauta_1_out_20), .col8(matrixauta_1_out_22),
    .col9(matrixauta_1_out_24), .col10(matrixauta_1_out_26), .col11(matrixauta_1_out_28),
    .col12(matrixauta_1_out_30));
  DotMatrix #(.matrixcols(2), .matrixrows(8)) dotmatrix_6 (.col0(matrixauta_1_out_5), .col1(matrixauta_1_out_8));
  DotMatrix #(.matrixcols(3), .matrixrows(3)) dotmatrix_7 (
    .col0(kod_1__2__cifra), .col1(kod_1__2__cifra_2), .col2(kod_1__2__cifra_3));
  DotMatrix #(.matrixcols(1), .matrixrows(3)) dotmatrix_8 ();  // open: col0
  DotMatrix #(.matrixcols(1), .matrixrows(3)) dotmatrix_9 ();  // open: col0
  DotMatrix #(.matrixcols(3), .matrixrows(3)) dotmatrix_10 (
    .col0(kod_1__3__cifra), .col1(kod_1__3__cifra_2), .col2(kod_1__3__cifra_3));
  Button u__5 (.out(_5_out));
  Button u__4 (.out(_4_out));
  Button u__6 (.out(_6_out));
  Button u__3 (.out(_3_out));
  Button button_1 (.out(_1));
  DotMatrix #(.matrixcols(3), .matrixrows(3)) dotmatrix_11 (
    .col0(kod_1__4__cifra), .col1(kod_1__4__cifra_2), .col2(kod_1__4__cifra_3));
  DotMatrix #(.matrixcols(3), .matrixrows(3)) dotmatrix_12 (
    .col0(kod_1_out_17), .col1(kod_1_out_19), .col2(kod_1_out_18));
  Button u__9 (.out(_9_out));
  Button u__8 (.out(_8_out));
  Button u__7 (.out(_7_out));
  Button button_2 (.out(_3));
  Button button_3 (.out(_2));
  Hex_Digit_Display hex_digit_display_4 (.value(_12));  // open: dp
  Hex_Digit_Display hex_digit_display_5 (.value(_11));  // open: dp
  Button P (.out(_16));
  functionality functionality_1 (
    .Button(_15), .\Otevírání (_7), .\Otevřeno (_8), .\Zavíraní (_9), .\Zavřeno (_10), .Desitky(_12),
    .Jednotky(_11), .LED(_24), .LOW(_1), .MEDIUM(_2), .HIGH(_3), .HIGH_2(_6), .MEDIUM_2(_5), .LOW_2(_4),
    .Pustit_Auto(_16), .AUTO___Desitky(_14), .AUTO___Jednotky(_13), .Pustit_Auto_2(_18), .in_2(_17),
    .Row_1(_27), .Row_2(_28), .Row_3(_29), .Row_4(_30), .Row_6(_32), .Row_7(_33), .Row_8(_34), .Row_5(_31),
    .Row_1_2(_35), .Row_2_2(_36), .Row_3_2(_37), .Row_4_2(_38), .Row_5_2(_39), .Row_6_2(_40), .Row_7_2(_41),
    .Row_8_2(_42));
  LED led_4 (.in(_24));
  Button button_4 (.out(_26));
  DotMatrix #(.inputtype("row"), .matrixcols(8), .matrixrows(8)) dotmatrix_13 (
    .row0(cabelmanagment_1_out_9), .row1(cabelmanagment_1_out_10), .row2(cabelmanagment_1_out_11),
    .row3(cabelmanagment_1_out_12), .row4(cabelmanagment_1_out_13), .row5(cabelmanagment_1_out_14),
    .row6(cabelmanagment_1_out_15), .row7(cabelmanagment_1_out_16));
  CabelManagment cabelmanagment_1 (
    .in_1(_27), .in_2(_28), .in_3(_29), .in_4(_30), .in_5(_31), .in_6(_32), .in_7(_33), .in_8(_34),
    .out_9(cabelmanagment_1_out_9), .out_10(cabelmanagment_1_out_10), .out_11(cabelmanagment_1_out_11),
    .out_12(cabelmanagment_1_out_12), .out_13(cabelmanagment_1_out_13), .out_14(cabelmanagment_1_out_14),
    .out_15(cabelmanagment_1_out_15), .out_16(cabelmanagment_1_out_16));
  DotMatrix #(.inputtype("row"), .matrixcols(8), .matrixrows(8)) dotmatrix_14 (
    .row0(cabelmanagment_2_out_16), .row1(cabelmanagment_2_out_15), .row2(cabelmanagment_2_out_14),
    .row3(cabelmanagment_2_out_13), .row4(cabelmanagment_2_out_12), .row5(cabelmanagment_2_out_11),
    .row6(cabelmanagment_2_out_10), .row7(cabelmanagment_2_out_9));
  CabelManagment cabelmanagment_2 (
    .in_1(_42), .in_2(_41), .in_3(_40), .in_4(_39), .in_5(_38), .in_6(_37), .in_7(_36), .in_8(_35),
    .out_9(cabelmanagment_2_out_9), .out_10(cabelmanagment_2_out_10), .out_11(cabelmanagment_2_out_11),
    .out_12(cabelmanagment_2_out_12), .out_13(cabelmanagment_2_out_13), .out_14(cabelmanagment_2_out_14),
    .out_15(cabelmanagment_2_out_15), .out_16(cabelmanagment_2_out_16));

  // Notes on the sheet:
  //   VRÁTNICE
  //   POČET AUT
  //   POKUSY
  //   START/STOP
  //   HZ: 8
  //   CASOVAČ
  //   PUSTIT AUTO
endmodule

module buttonswitch (
  input  Odemceno,
  input  Reset,
  input  Button,
  output \Output___Otevřeno_Zavřeno 
);

  wire and_1_out, d_ff_1_qn, d_ff_2_q, or_1_out;

  or or_1 (or_1_out, Button, Reset);
  and and_1 (and_1_out, or_1_out, Odemceno);
  D_Flip_Flop #(.trigger("high")) d_ff_1 (
    .clk(and_1_out), .D(d_ff_2_q), .Q(\Output___Otevřeno_Zavřeno ), .Qn(d_ff_1_qn));  // open: preset, en, reset
  D_Flip_Flop d_ff_2 (.clk(and_1_out), .D(d_ff_1_qn), .Q(d_ff_2_q));  // open: Qn, preset, en, reset
endmodule

module reset (
  input  Leva_Zavirani,
  input  Leva_Zavreno,
  input  Zavrit,
  input  CLOCK,
  output OUTPUT___RESET
);

  wire and_1_out;

  and and_1 (and_1_out, Leva_Zavirani, Leva_Zavreno, Zavrit);
  Counter #(.width(1), .max('h1), .trigger("falling")) counter_1 (
    .count(and_1_out), .carry(OUTPUT___RESET), .clk(CLOCK), .clr(OUTPUT___RESET));  // open: load, D, Q
endmodule

module functionality (
  input  Button,
  input  in_2,
  input  LOW,
  input  MEDIUM,
  input  HIGH,
  input  Pustit_Auto,
  output [3:0] Desitky,
  output [3:0] Jednotky,
  output LED,
  output HIGH_2,
  output MEDIUM_2,
  output LOW_2,
  output \Otevírání ,
  output [7:0] Row_1,
  output [7:0] Row_2,
  output \Otevřeno ,
  output [7:0] Row_3,
  output \Zavíraní ,
  output [7:0] Row_4,
  output [7:0] Row_5,
  output \Zavřeno ,
  output [7:0] Row_6,
  output [7:0] Row_7,
  output [7:0] Row_8,
  output [7:0] Row_1_2,
  output [3:0] AUTO___Desitky,
  output [7:0] Row_2_2,
  output Pustit_Auto_2,
  output [7:0] Row_3_2,
  output [3:0] AUTO___Jednotky,
  output [7:0] Row_4_2,
  output [7:0] Row_5_2,
  output [7:0] Row_6_2,
  output [7:0] Row_7_2,
  output [7:0] Row_8_2
);

  wire and_1_out, and_2_out, and_3_out, and_4_out, and_5_out, and_6_out, AR, AUTO_RESET, BR, clock_1_out,
       clock_2_out, comparator_1_eq, comparator_2_gt, comparator_3_lt, counter_3_carry, CR, LO, not_1_out,
       or_1_out, or_2_out, PO, rychlostswitch_1_clock_output, VZ, ZP, ZT;
  wire [2:0] LH, PH;
  wire [4:0] counter_3_q;

  or or_1 (or_1_out, AUTO_RESET, BR);
  and and_1 (and_1_out, ZP, in_2);
  rychlostswitch rychlostswitch_1 (
    .Clock_output(rychlostswitch_1_clock_output), .LOW(LOW), .MEDIUM(MEDIUM), .HIGH(HIGH), .HIGH_2(HIGH_2),
    .MEDIUM_2(MEDIUM_2), .LOW_2(LOW_2));
  Comparator #(.width(3), .mode("unsigned")) comparator_1 (.a(PH), .b(3'b111), .eq(comparator_1_eq));  // open: gt, lt
  auta auta_1 (
    .Button___Pustit(Pustit_Auto), .\Otevřeno (comparator_1_eq), .\Desítky (AUTO___Desitky),
    .Jednotky(AUTO___Jednotky), .Pusteni_povoleno(Pustit_Auto_2), .\Zavrení_povoleno (ZP));
  buttonswitch buttonswitch_1 (
    .Reset(Button), .\Output___Otevřeno_Zavřeno (VZ), .Button(or_1_out), .Odemceno(and_1_out));
  display display_1 (
    .\Otevírání (\Otevírání ), .\Pravá_Otevřeno (PO), .\Otevřeno (\Otevřeno ), .\Levá_otevřeno (LO),
    .\Zavřít (ZT), .\Zavírání (\Zavíraní ), .Zapnuto_Vypnuto(VZ), .\Zavřeno (\Zavřeno ), .in_5(LH));
  and and_2 (and_2_out, and_5_out, comparator_3_lt);
  and and_3 (and_3_out, VZ, rychlostswitch_1_clock_output);
  Counter #(.width(3), .max('h7), .ongoal("stay"), .trigger("falling")) counter_1 (
    .load(and_2_out), .Q(LH), .carry(LO), .clk(and_3_out));  // open: D, count, clr
  zavritdriv zavritdriv_1 (
    .Hodnota_otevreni_zleva(LH), .On_Off(VZ), .Zavrit_driv(AR), .Button_reset(BR), .Casovac_reset(CR),
    .Auto_Reset(AUTO_RESET));
  Comparator #(.width(3), .mode("unsigned")) comparator_2 (.a(LH), .b(3'b011), .gt(comparator_2_gt));  // open: eq, lt
  reset reset_1 (
    .Leva_Zavirani(LO), .Leva_Zavreno(and_2_out), .Zavrit(and_5_out), .OUTPUT___RESET(AUTO_RESET),
    .CLOCK(rychlostswitch_1_clock_output));
  and and_4 (and_4_out, comparator_2_gt, VZ, rychlostswitch_1_clock_output);
  Counter #(.width(3), .max('h7), .ongoal("stay"), .trigger("falling")) counter_2 (
    .load(and_5_out), .Q(PH), .carry(PO), .clk(and_4_out));  // open: D, count, clr
  Comparator #(.width(3), .mode("unsigned")) comparator_3 (.a(PH), .b(3'b100), .lt(comparator_3_lt));  // open: gt, eq
  Clock #(.highDuration(4), .lowDuration(4)) clock_1 (.out(clock_1_out));
  and and_5 (and_5_out, ZT, ZP);
  and and_6 (and_6_out, PO, VZ, clock_1_out);
  Counter #(.width(5), .max('h1e), .ongoal("stay")) counter_3 (
    .Q(counter_3_q), .carry(counter_3_carry), .clk(and_6_out), .clr(or_2_out));  // open: load, D, count
  or or_2 (or_2_out, CR, AUTO_RESET);
  MatrixVrata matrixvrata_1 (
    .out_5(Row_1), .out_6(Row_2), .out_7(Row_3), .out_8(Row_4), .out_9(Row_5), .out_10(Row_6),
    .out_11(Row_7), .out_12(Row_8), .in_1(LH), .in_2(rychlostswitch_1_clock_output), .in_3(PH),
    .out_13(Row_1_2), .out_14(Row_2_2), .out_15(Row_3_2), .out_16(Row_4_2), .out_17(Row_5_2),
    .out_18(Row_6_2), .out_19(Row_7_2), .out_20(Row_8_2), .in_4(rychlostswitch_1_clock_output));
  or or_3 (ZT, counter_3_carry, AR);
  and and_7 (LED, VZ, clock_2_out);
  Clock #(.highDuration(3), .lowDuration(3)) clock_2 (.out(clock_2_out));
  hexdisplaycasovac hexdisplaycasovac_1 (.in_1(counter_3_q), .desitky(Desitky), .Jednotky(Jednotky), .in_2(not_1_out));
  not not_1 (not_1_out, AR);

  // Other names for the same wires on the sheet: Zavreno = \Zavřeno 
endmodule

module display (
  input  \Pravá_Otevřeno ,
  input  \Levá_otevřeno ,
  input  \Zavřít ,
  input  Zapnuto_Vypnuto,
  input  [2:0] in_5,
  output \Otevírání ,
  output \Otevřeno ,
  output \Zavírání ,
  output \Zavřeno 
);

  wire and_2_out, and_3_out, and_4_out, and_6_out, comparator_1_eq, not_1_out, not_2_out, not_3_out,
       not_4_out, not_5_out;

  Comparator #(.width(3), .mode("unsigned")) comparator_1 (.a(in_5), .b(3'b000), .eq(comparator_1_eq));  // open: gt, lt
  not not_1 (not_1_out, \Zavřít );
  not not_2 (not_2_out, \Pravá_Otevřeno );
  not not_3 (not_3_out, \Zavřít );
  not not_4 (not_4_out, \Pravá_Otevřeno );
  not not_5 (not_5_out, \Levá_otevřeno );
  and and_1 (\Otevírání , Zapnuto_Vypnuto, not_1_out, not_2_out);
  and and_2 (and_2_out, \Pravá_Otevřeno , not_3_out);
  and and_3 (and_3_out, not_4_out, \Zavřít );
  and and_4 (and_4_out, not_5_out, \Zavřít );
  and and_5 (\Zavřeno , ~Zapnuto_Vypnuto, comparator_1_eq);  // AND_Gate
  or or_1 (\Zavírání , and_3_out, and_4_out);
  or or_2 (\Otevřeno , and_2_out, and_6_out);
  and and_6 (and_6_out, ~\Otevírání , ~\Zavírání , ~\Zavřeno );  // AND_Gate
endmodule

module zavritdriv (
  input  [2:0] Hodnota_otevreni_zleva,
  input  On_Off,
  input  Auto_Reset,
  output Zavrit_driv,
  output Button_reset,
  output Casovac_reset
);

  wire and_1_out, comparator_1_eq, comparator_1_gt, counter_1_carry, or_1_out;

  or or_1 (or_1_out, and_1_out, Button_reset, Auto_Reset);
  and and_1 (and_1_out, ~On_Off, counter_1_carry);  // AND_Gate
  Comparator #(.width(3), .mode("unsigned")) comparator_1 (
    .a(Hodnota_otevreni_zleva), .b(3'b000), .gt(comparator_1_gt), .eq(comparator_1_eq));  // open: lt
  Counter #(.width(2), .max('h2), .ongoal("stay")) counter_1 (
    .carry(counter_1_carry), .clk(On_Off), .clr(or_1_out));  // open: load, D, count, Q
  and and_2 (Zavrit_driv, comparator_1_gt, counter_1_carry);
  and and_3 (Button_reset, comparator_1_eq, counter_1_carry);
  or or_2 (Casovac_reset, Button_reset, and_1_out);
endmodule

module MatrixVrata (
  input  [2:0] in_1,
  input  in_2,
  input  [2:0] in_3,
  input  in_4,
  output [7:0] out_5,
  output [7:0] out_6,
  output [7:0] out_7,
  output [7:0] out_8,
  output [7:0] out_9,
  output [7:0] out_10,
  output [7:0] out_11,
  output [7:0] out_12,
  output [7:0] out_13,
  output [7:0] out_14,
  output [7:0] out_15,
  output [7:0] out_16,
  output [7:0] out_17,
  output [7:0] out_18,
  output [7:0] out_19,
  output [7:0] out_20
);

  wire [7:0] rendering_1_out_3, rendering_2_out_3, rendering_3_out_3, rendering_4_out_3, rendering_5_out_3,
       rendering_6_out_3, rendering_7_out_3, rendering_8_out_3, renderingright_1_out_3,
       renderingright_2_out_3, renderingright_3_out_3, renderingright_4_out_3, renderingright_5_out_3,
       renderingright_6_out_3, renderingright_7_out_3, renderingright_8_out_3;

  rendering rendering_1 (.in_1(8'h1), .in_2(in_1), .out_3(rendering_1_out_3));
  rendering rendering_2 (.in_1(8'h7), .in_2(in_1), .out_3(rendering_2_out_3));
  rendering rendering_3 (.in_1(8'h7d), .in_2(in_1), .out_3(rendering_3_out_3));
  rendering rendering_4 (.in_1(8'h55), .in_2(in_1), .out_3(rendering_4_out_3));
  rendering rendering_5 (.in_1(8'hd5), .in_2(in_1), .out_3(rendering_5_out_3));
  rendering rendering_6 (.in_1(8'h95), .in_2(in_1), .out_3(rendering_6_out_3));
  rendering rendering_7 (.in_1(8'h95), .in_2(in_1), .out_3(rendering_7_out_3));
  rendering rendering_8 (.in_1({8{1'b1}}), .in_2(in_1), .out_3(rendering_8_out_3));
  renderingright renderingright_1 (.in_1(8'h80), .in_2(in_3), .out_3(renderingright_1_out_3));
  renderingright renderingright_2 (.in_1(8'he0), .in_2(in_3), .out_3(renderingright_2_out_3));
  renderingright renderingright_3 (.in_1(8'hbe), .in_2(in_3), .out_3(renderingright_3_out_3));
  renderingright renderingright_4 (.in_1(8'haa), .in_2(in_3), .out_3(renderingright_4_out_3));
  renderingright renderingright_5 (.in_1(8'hab), .in_2(in_3), .out_3(renderingright_5_out_3));
  renderingright renderingright_6 (.in_1(8'ha9), .in_2(in_3), .out_3(renderingright_6_out_3));
  renderingright renderingright_7 (.in_1(8'ha9), .in_2(in_3), .out_3(renderingright_7_out_3));
  renderingright renderingright_8 (.in_1({8{1'b1}}), .in_2(in_3), .out_3(renderingright_8_out_3));
  RAM #(.addrWidth(3), .bus("separate")) ram_1 (
    .addr(in_1), .din(rendering_1_out_3), .data(out_5), .clk(in_2));  // open: str, sel, ld, clr
  RAM #(.addrWidth(3), .bus("separate")) ram_2 (
    .addr(in_1), .din(rendering_2_out_3), .data(out_6), .clk(in_2));  // open: str, sel, ld, clr
  RAM #(.addrWidth(3), .bus("separate")) ram_3 (
    .addr(in_1), .din(rendering_3_out_3), .data(out_7), .clk(in_2));  // open: str, sel, ld, clr
  RAM #(.addrWidth(3), .bus("separate")) ram_4 (
    .addr(in_1), .din(rendering_4_out_3), .data(out_8), .clk(in_2));  // open: str, sel, ld, clr
  RAM #(.addrWidth(3), .bus("separate")) ram_5 (
    .addr(in_1), .din(rendering_5_out_3), .data(out_9), .clk(in_2));  // open: str, sel, ld, clr
  RAM #(.addrWidth(3), .bus("separate")) ram_6 (
    .addr(in_1), .din(rendering_6_out_3), .data(out_10), .clk(in_2));  // open: str, sel, ld, clr
  RAM #(.addrWidth(3), .bus("separate")) ram_7 (
    .addr(in_1), .din(rendering_7_out_3), .data(out_11), .clk(in_2));  // open: str, sel, ld, clr
  RAM #(.addrWidth(3), .bus("separate")) ram_8 (
    .addr(in_1), .din(rendering_8_out_3), .data(out_12), .clk(in_2));  // open: str, sel, ld, clr
  RAM #(.addrWidth(3), .bus("separate")) ram_9 (
    .addr(in_3), .din(renderingright_1_out_3), .data(out_13), .clk(in_4));  // open: str, sel, ld, clr
  RAM #(.addrWidth(3), .bus("separate")) ram_10 (
    .addr(in_3), .din(renderingright_2_out_3), .data(out_14), .clk(in_4));  // open: str, sel, ld, clr
  RAM #(.addrWidth(3), .bus("separate")) ram_11 (
    .addr(in_3), .din(renderingright_3_out_3), .data(out_15), .clk(in_4));  // open: str, sel, ld, clr
  RAM #(.addrWidth(3), .bus("separate")) ram_12 (
    .addr(in_3), .din(renderingright_4_out_3), .data(out_16), .clk(in_4));  // open: str, sel, ld, clr
  RAM #(.addrWidth(3), .bus("separate")) ram_13 (
    .addr(in_3), .din(renderingright_5_out_3), .data(out_17), .clk(in_4));  // open: str, sel, ld, clr
  RAM #(.addrWidth(3), .bus("separate")) ram_14 (
    .addr(in_3), .din(renderingright_6_out_3), .data(out_18), .clk(in_4));  // open: str, sel, ld, clr
  RAM #(.addrWidth(3), .bus("separate")) ram_15 (
    .addr(in_3), .din(renderingright_7_out_3), .data(out_19), .clk(in_4));  // open: str, sel, ld, clr
  RAM #(.addrWidth(3), .bus("separate")) ram_16 (
    .addr(in_3), .din(renderingright_8_out_3), .data(out_20), .clk(in_4));  // open: str, sel, ld, clr
endmodule

module hexdisplaycasovac (
  input  [4:0] in_1,
  input  in_2,
  output [3:0] desitky,
  output [3:0] Jednotky
);

  wire and_1_out, and_2_out, comparator_1_eq, comparator_1_gt, comparator_1_lt, comparator_2_gt,
       comparator_3_gt, or_1_out, subtractor_2_bout, subtractor_3_bout;
  wire [4:0] controlled_buffer_1_out, subtractor_1_out, subtractor_2_out, subtractor_3_out, subtractor_4_out;
  wire [4:4] controlled_buffer_6_out;

  Subtractor #(.width(5)) subtractor_1 (.a(5'b11110), .b(in_1), .out(subtractor_1_out));  // open: bin, bout
  assign controlled_buffer_1_out = in_2 ? subtractor_1_out : 5'bz;  // Controlled_Buffer controlled_buffer_1
  Comparator #(.width(5), .mode("unsigned")) comparator_1 (
    .a(controlled_buffer_1_out), .b(5'b01001), .gt(comparator_1_gt), .eq(comparator_1_eq),
    .lt(comparator_1_lt));
  Comparator #(.width(5), .mode("unsigned")) comparator_2 (
    .a(controlled_buffer_1_out), .b(5'b10011), .gt(comparator_2_gt));  // open: eq, lt
  Comparator #(.width(5), .mode("unsigned")) comparator_3 (
    .a(controlled_buffer_1_out), .b(5'b11101), .gt(comparator_3_gt));  // open: eq, lt
  Subtractor #(.width(5)) subtractor_2 (
    .a(controlled_buffer_1_out), .b(5'b01010), .out(subtractor_2_out), .bout(subtractor_2_bout));  // open: bin
  Subtractor #(.width(5)) subtractor_3 (
    .a(controlled_buffer_1_out), .b(5'b10100), .out(subtractor_3_out), .bin(subtractor_2_bout),
    .bout(subtractor_3_bout));
  Subtractor #(.width(5)) subtractor_4 (
    .a(controlled_buffer_1_out), .b(5'b11110), .out(subtractor_4_out), .bin(subtractor_3_bout));  // open: bout
  or or_1 (or_1_out, comparator_1_lt, comparator_1_eq);
  and and_1 (and_1_out, comparator_1_gt, ~comparator_2_gt);  // AND_Gate
  and and_2 (and_2_out, comparator_2_gt, ~comparator_3_gt);  // AND_Gate
  assign desitky = or_1_out ? 4'b0000 : 4'bz;  // Controlled_Buffer controlled_buffer_2
  assign desitky = and_1_out ? 4'b0001 : 4'bz;  // Controlled_Buffer controlled_buffer_3
  assign desitky = and_2_out ? 4'b0010 : 4'bz;  // Controlled_Buffer controlled_buffer_4
  assign desitky = comparator_3_gt ? 4'b0011 : 4'bz;  // Controlled_Buffer controlled_buffer_5
  assign {controlled_buffer_6_out[4], Jednotky} = or_1_out ? controlled_buffer_1_out : 5'bz;  // Controlled_Buffer controlled_buffer_6
  assign {controlled_buffer_6_out[4], Jednotky} = and_1_out ? subtractor_2_out : 5'bz;  // Controlled_Buffer controlled_buffer_7
  assign {controlled_buffer_6_out[4], Jednotky} = and_2_out ? subtractor_3_out : 5'bz;  // Controlled_Buffer controlled_buffer_8
  assign {controlled_buffer_6_out[4], Jednotky} = comparator_3_gt ? subtractor_4_out : 5'bz;  // Controlled_Buffer controlled_buffer_9
  // also tied to GND on the sheet: controlled_buffer_6_out[4]
endmodule

module stavbranydisplay (
  input  \Otevřeno ,
  input  \Zavřeno ,
  input  \Otevírání ,
  input  \Zavírání ,
  output [31:0] \_1__Řádek ,
  output [31:0] \_2__Řádek ,
  output [31:0] \_3__Řádek ,
  output [31:0] \_4__Řádek ,
  output [31:0] \_5__Řádek 
);

  assign \_1__Řádek  = \Zavírání  ? 32'hf32ae64a : 32'bz;  // Controlled_Buffer controlled_buffer_1
  assign \_1__Řádek  = \Otevírání  ? 32'heeeab925 : 32'bz;  // Controlled_Buffer controlled_buffer_2
  assign \_1__Řádek  = \Zavřeno  ? 32'hf32bba5e : 32'bz;  // Controlled_Buffer controlled_buffer_3
  assign \_1__Řádek  = \Otevřeno  ? 32'heeeaee97 : 32'bz;  // Controlled_Buffer controlled_buffer_4
  assign \_2__Řádek  = \Zavírání  ? 32'h24aaa96a : 32'bz;  // Controlled_Buffer controlled_buffer_5
  assign \_2__Řádek  = \Otevírání  ? 32'ha48aaab5 : 32'bz;  // Controlled_Buffer controlled_buffer_6
  assign \_2__Řádek  = \Zavřeno  ? 32'h24aaa352 : 32'bz;  // Controlled_Buffer controlled_buffer_7
  assign \_2__Řádek  = \Otevřeno  ? 32'ha48aa8d5 : 32'bz;  // Controlled_Buffer controlled_buffer_8
  assign \_3__Řádek  = \Zavírání  ? 32'h47aacf5a : 32'bz;  // Controlled_Buffer controlled_buffer_9
  assign \_3__Řádek  = \Otevírání  ? 32'ha4cab3ad : 32'bz;  // Controlled_Buffer controlled_buffer_10
  assign \_3__Řádek  = \Zavřeno  ? 32'h47ab32d2 : 32'bz;  // Controlled_Buffer controlled_buffer_11
  assign \_3__Řádek  = \Otevřeno  ? 32'ha4caccb5 : 32'bz;  // Controlled_Buffer controlled_buffer_12
  assign \_4__Řádek  = \Zavírání  ? 32'h84aaa95a : 32'bz;  // Controlled_Buffer controlled_buffer_13
  assign \_4__Řádek  = \Otevírání  ? 32'ha48aaaad : 32'bz;  // Controlled_Buffer controlled_buffer_14
  assign \_4__Řádek  = \Zavřeno  ? 32'h84aaa2d2 : 32'bz;  // Controlled_Buffer controlled_buffer_15
  assign \_4__Řádek  = \Otevřeno  ? 32'ha48aa8b5 : 32'bz;  // Controlled_Buffer controlled_buffer_16
  assign \_5__Řádek  = \Zavírání  ? 32'hf492a94a : 32'bz;  // Controlled_Buffer controlled_buffer_17
  assign \_5__Řádek  = \Otevírání  ? 32'he4e4aaa5 : 32'bz;  // Controlled_Buffer controlled_buffer_18
  assign \_5__Řádek  = \Zavřeno  ? 32'hf492ba5e : 32'bz;  // Controlled_Buffer controlled_buffer_19
  assign \_5__Řádek  = \Otevřeno  ? 32'he4e4ae97 : 32'bz;  // Controlled_Buffer controlled_buffer_20
  DotMatrix #(.inputtype("row"), .matrixcols(32), .matrixrows(5)) dotmatrix_1 (
    .row0(32'heeeaee97), .row1(32'ha48aa8d5), .row2(32'ha4caccb5), .row3(32'ha48aa8b5), .row4(32'he4e4ae97));
  DotMatrix #(.inputtype("row"), .matrixcols(32), .matrixrows(5)) dotmatrix_2 (
    .row0(32'hf32bba5e), .row1(32'h24aaa352), .row2(32'h47ab32d2), .row3(32'h84aaa2d2), .row4(32'hf492ba5e));
  DotMatrix #(.inputtype("row"), .matrixcols(32), .matrixrows(5)) dotmatrix_3 (
    .row0(32'heeeab925), .row1(32'ha48aaab5), .row2(32'ha4cab3ad), .row3(32'ha48aaaad), .row4(32'he4e4aaa5));
  DotMatrix #(.inputtype("row"), .matrixcols(32), .matrixrows(5)) dotmatrix_4 (
    .row0(32'hf32ae64a), .row1(32'h24aaa96a), .row2(32'h47aacf5a), .row3(32'h84aaa95a), .row4(32'hf492a94a));

  // Notes on the sheet:
  //   Otevřeno - Matrix text
  //   Zavřeno - Matrix Text
  //   Otevírání - Matrix Text
  //   Zavírání - Matrix Text
endmodule

module rychlostswitch (
  input  HIGH,
  input  MEDIUM,
  input  LOW,
  output Clock_output,
  output HIGH_2,
  output MEDIUM_2,
  output LOW_2
);

  wire and_1_out, clock_1_out, clock_2_out, clock_3_out, d_ff_1_qn, d_ff_2_q, d_ff_2_qn, d_ff_3_qn, or_1_out,
       or_2_out, or_3_out;
  wire [1:0] controlled_buffer_1_out;

  Clock clock_1 (.out(clock_1_out));
  Clock #(.highDuration(2), .lowDuration(2)) clock_2 (.out(clock_2_out));
  Clock #(.highDuration(4), .lowDuration(4)) clock_3 (.out(clock_3_out));
  or or_1 (or_1_out, HIGH, MEDIUM, LOW);
  or or_2 (or_2_out, HIGH, MEDIUM, LOW);
  or or_3 (or_3_out, HIGH, MEDIUM, LOW);
  D_Flip_Flop d_ff_1 (.clk(or_1_out), .D(HIGH), .Q(HIGH_2), .Qn(d_ff_1_qn));  // open: preset, en, reset
  D_Flip_Flop d_ff_2 (.clk(or_2_out), .D(MEDIUM), .Q(d_ff_2_q), .Qn(d_ff_2_qn));  // open: preset, en, reset
  D_Flip_Flop d_ff_3 (.clk(or_3_out), .D(LOW), .Q(LOW_2), .Qn(d_ff_3_qn));  // open: preset, en, reset
  assign controlled_buffer_1_out = HIGH_2 ? 2'b00 : 2'bz;  // Controlled_Buffer controlled_buffer_1
  assign controlled_buffer_1_out = d_ff_2_q ? 2'b01 : 2'bz;  // Controlled_Buffer controlled_buffer_2
  assign controlled_buffer_1_out = LOW_2 ? 2'b10 : 2'bz;  // Controlled_Buffer controlled_buffer_3
  assign controlled_buffer_1_out = and_1_out ? 2'b01 : 2'bz;  // Controlled_Buffer controlled_buffer_4
  and and_1 (and_1_out, d_ff_1_qn, d_ff_2_qn, d_ff_3_qn);
  Multiplexer #(.select(2), .enable("false")) multiplexer_1 (
    .in0(clock_1_out), .in1(clock_2_out), .in2(clock_3_out), .out(Clock_output), .sel(controlled_buffer_1_out));  // open: in3
  or or_4 (MEDIUM_2, d_ff_2_q, and_1_out);
endmodule

module auta (
  input  Button___Pustit,
  input  \Otevřeno ,
  output [3:0] \Desítky ,
  output [3:0] Jednotky,
  output Pusteni_povoleno,
  output \Zavrení_povoleno 
);

  wire and_1_out, CL, counter_3_carry, nor_1_out, or_1_out, or_2_out, undriven, xor_1_out, xor_2_out,
       xor_3_out, xor_4_out;
  wire [3:0] random_1_out;
  wire [4:0] counter_2_q;

  Clock #(.highDuration(3), .lowDuration(4)) clock_1 (.out(CL));
  Random #(.width(4)) random_1 (.clk(CL), .out(random_1_out), .clr(undriven));  // open: next
  xor xor_1 (xor_1_out, random_1_out[0], 1'b1);
  xor xor_2 (xor_2_out, random_1_out[1], 1'b1);
  xor xor_3 (xor_3_out, random_1_out[2], 1'b1);
  xor xor_4 (xor_4_out, random_1_out[3], 1'b1);
  nor nor_1 (nor_1_out, xor_1_out, xor_2_out, xor_3_out, xor_4_out);
  and and_1 (and_1_out, Button___Pustit, counter_3_carry, \Otevřeno );
  or or_1 (or_1_out, nor_1_out, and_1_out);
  Counter #(.width(4), .max('h9), .ongoal("stay")) counter_1 (
    .carry(\Zavrení_povoleno ), .clk(CL), .clr(and_1_out));  // open: load, D, count, Q
  Counter #(.width(5), .max('h1f), .ongoal("stay")) counter_2 (
    .load(and_1_out), .count(or_1_out), .Q(counter_2_q), .clk(or_1_out));  // open: D, carry, clr
  Counter #(.width(3), .max('h5), .ongoal("stay")) counter_3 (
    .carry(counter_3_carry), .clk(CL), .clr(and_1_out));  // open: load, D, count, Q
  hexdisplayauta hexdisplayauta_1 (.in_1(counter_2_q), .desitky(\Desítky ), .Jednotky(Jednotky));
  or or_2 (or_2_out, counter_2_q[0], counter_2_q[1], counter_2_q[2], counter_2_q[3], counter_2_q[4]);
  and and_2 (Pusteni_povoleno, counter_3_carry, or_2_out, \Otevřeno );
endmodule

module hexdisplayauta (
  input  [4:0] in_1,
  output [3:0] desitky,
  output [3:0] Jednotky
);

  wire and_1_out, and_2_out, comparator_1_eq, comparator_1_gt, comparator_1_lt, comparator_2_gt,
       comparator_3_gt, or_1_out, subtractor_1_bout, subtractor_2_bout;
  wire [4:0] subtractor_1_out, subtractor_2_out, subtractor_3_out;
  wire [4:4] controlled_buffer_5_out;

  Comparator #(.width(5), .mode("unsigned")) comparator_1 (
    .a(in_1), .b(5'b01001), .gt(comparator_1_gt), .eq(comparator_1_eq), .lt(comparator_1_lt));
  Comparator #(.width(5), .mode("unsigned")) comparator_2 (
    .a(in_1), .b(5'b10011), .gt(comparator_2_gt));  // open: eq, lt
  Comparator #(.width(5), .mode("unsigned")) comparator_3 (
    .a(in_1), .b(5'b11101), .gt(comparator_3_gt));  // open: eq, lt
  Subtractor #(.width(5)) subtractor_1 (
    .a(in_1), .b(5'b01010), .out(subtractor_1_out), .bout(subtractor_1_bout));  // open: bin
  Subtractor #(.width(5)) subtractor_2 (
    .a(in_1), .b(5'b10100), .out(subtractor_2_out), .bin(subtractor_1_bout), .bout(subtractor_2_bout));
  Subtractor #(.width(5)) subtractor_3 (
    .a(in_1), .b(5'b11110), .out(subtractor_3_out), .bin(subtractor_2_bout));  // open: bout
  or or_1 (or_1_out, comparator_1_lt, comparator_1_eq);
  and and_1 (and_1_out, comparator_1_gt, ~comparator_2_gt);  // AND_Gate
  and and_2 (and_2_out, comparator_2_gt, ~comparator_3_gt);  // AND_Gate
  assign desitky = or_1_out ? 4'b0000 : 4'bz;  // Controlled_Buffer controlled_buffer_1
  assign desitky = and_1_out ? 4'b0001 : 4'bz;  // Controlled_Buffer controlled_buffer_2
  assign desitky = and_2_out ? 4'b0010 : 4'bz;  // Controlled_Buffer controlled_buffer_3
  assign desitky = comparator_3_gt ? 4'b0011 : 4'bz;  // Controlled_Buffer controlled_buffer_4
  assign {controlled_buffer_5_out[4], Jednotky} = or_1_out ? in_1 : 5'bz;  // Controlled_Buffer controlled_buffer_5
  assign {controlled_buffer_5_out[4], Jednotky} = and_1_out ? subtractor_1_out : 5'bz;  // Controlled_Buffer controlled_buffer_6
  assign {controlled_buffer_5_out[4], Jednotky} = and_2_out ? subtractor_2_out : 5'bz;  // Controlled_Buffer controlled_buffer_7
  assign {controlled_buffer_5_out[4], Jednotky} = comparator_3_gt ? subtractor_3_out : 5'bz;  // Controlled_Buffer controlled_buffer_8
  // also tied to GND on the sheet: controlled_buffer_5_out[4]
endmodule

module kod (
  input  _7,
  input  _8,
  input  _9,
  input  _4,
  input  _5,
  input  _6,
  input  _1,
  input  _2,
  input  _3,
  input  C,
  input  _0,
  input  OK,
  input  Force_reset,
  input  Zavreno,
  output [3:0] out_15,
  output \Odemknuto_Zamčeno ,
  output [2:0] out_17,
  output [2:0] out_18,
  output [2:0] out_19,
  output [2:0] _1__Cifra,
  output [2:0] _1__Cifra_2,
  output [2:0] _1__Cifra_3,
  output [2:0] _2__Cifra,
  output [2:0] _2__Cifra_2,
  output [2:0] _2__Cifra_3,
  output [2:0] _3__Cifra,
  output [2:0] _3__Cifra_2,
  output [2:0] _3__Cifra_3,
  output [2:0] _4__Cifra,
  output [2:0] _4__Cifra_2,
  output [2:0] _4__Cifra_3
);

  wire and_1_out, and_2_out, comparator_1_eq, comparator_2_eq, comparator_3_eq, comparator_4_eq,
       counter_2_carry, demultiplexer_1_out0, demultiplexer_1_out1, demultiplexer_1_out2,
       demultiplexer_1_out3, Limit, or_1_out, or_2_out, or_3_out, or_4_out, or_5_out, or_6_out, or_7_out,
       s_r_ff_1_q, s_r_ff_2_q, s_r_ff_3_q, s_r_ff_4_q;
  wire [1:0] counter_1_q, counter_2_q;
  wire [3:0] controlled_buffer_1_out, n4bitmemory_1_out_5, n4bitmemory_2_out_5, n4bitmemory_3_out_5,
       n4bitmemory_4_out_5;

  or or_1 (or_1_out, C, OK);
  or or_2 (or_2_out, _2, _1, _4, _7, _0, _5, _8, _3, _6, _9);
  assign controlled_buffer_1_out = _9 ? 4'b1001 : 4'bz;  // Controlled_Buffer controlled_buffer_1
  assign controlled_buffer_1_out = _8 ? 4'b1000 : 4'bz;  // Controlled_Buffer controlled_buffer_2
  assign controlled_buffer_1_out = _7 ? 4'b0111 : 4'bz;  // Controlled_Buffer controlled_buffer_3
  assign controlled_buffer_1_out = _6 ? 4'b0110 : 4'bz;  // Controlled_Buffer controlled_buffer_4
  assign controlled_buffer_1_out = _5 ? 4'b0101 : 4'bz;  // Controlled_Buffer controlled_buffer_5
  assign controlled_buffer_1_out = _4 ? 4'b0100 : 4'bz;  // Controlled_Buffer controlled_buffer_6
  assign controlled_buffer_1_out = _3 ? 4'b0011 : 4'bz;  // Controlled_Buffer controlled_buffer_7
  assign controlled_buffer_1_out = _2 ? 4'b0010 : 4'bz;  // Controlled_Buffer controlled_buffer_8
  assign controlled_buffer_1_out = _1 ? 4'b0001 : 4'bz;  // Controlled_Buffer controlled_buffer_9
  assign controlled_buffer_1_out = _0 ? 4'b0000 : 4'bz;  // Controlled_Buffer controlled_buffer_10
  Demultiplexer #(.select(2), .enable("false")) demultiplexer_1 (
    .out0(demultiplexer_1_out0), .out1(demultiplexer_1_out1), .out2(demultiplexer_1_out2),
    .out3(demultiplexer_1_out3), .in(1'b1), .sel(counter_1_q));
  Counter #(.width(2), .max('h3), .ongoal("stay"), .trigger("falling")) counter_1 (
    .Q(counter_1_q), .clk(or_2_out), .clr(or_1_out));  // open: load, D, count, carry
  _4bitmemory u_4bitmemory_1 (
    .out_5(n4bitmemory_1_out_5), .Input(controlled_buffer_1_out), .in_2(demultiplexer_1_out0),
    .in_3(or_2_out), .RESET(or_1_out));
  _4bitmemory u_4bitmemory_2 (
    .out_5(n4bitmemory_2_out_5), .Input(controlled_buffer_1_out), .in_2(demultiplexer_1_out1),
    .in_3(or_2_out), .RESET(or_1_out));
  _4bitmemory u_4bitmemory_3 (
    .out_5(n4bitmemory_3_out_5), .Input(controlled_buffer_1_out), .in_2(demultiplexer_1_out2),
    .in_3(or_2_out), .RESET(or_1_out));
  _4bitmemory u_4bitmemory_4 (
    .out_5(n4bitmemory_4_out_5), .Input(controlled_buffer_1_out), .in_2(demultiplexer_1_out3),
    .in_3(or_2_out), .RESET(or_1_out));
  Comparator #(.width(4), .mode("unsigned")) comparator_1 (
    .a(4'b0110), .b(n4bitmemory_1_out_5), .eq(comparator_1_eq));  // open: gt, lt
  Comparator #(.width(4), .mode("unsigned")) comparator_2 (
    .a(4'b0011), .b(n4bitmemory_2_out_5), .eq(comparator_2_eq));  // open: gt, lt
  Comparator #(.width(4), .mode("unsigned")) comparator_3 (
    .a(4'b1001), .b(n4bitmemory_3_out_5), .eq(comparator_3_eq));  // open: gt, lt
  Comparator #(.width(4), .mode("unsigned")) comparator_4 (
    .a(4'b0000), .b(n4bitmemory_4_out_5), .eq(comparator_4_eq));  // open: gt, lt
  or or_3 (or_3_out, demultiplexer_1_out0, or_1_out);
  or or_4 (or_4_out, demultiplexer_1_out1, or_1_out);
  or or_5 (or_5_out, demultiplexer_1_out2, or_1_out);
  or or_6 (or_6_out, demultiplexer_1_out3, or_1_out);
  S_R_Flip_Flop #(.trigger("high")) s_r_ff_1 (
    .S(or_2_out), .clk(or_3_out), .R(or_1_out), .Q(s_r_ff_1_q));  // open: Qn, preset, reset, en
  S_R_Flip_Flop #(.trigger("high")) s_r_ff_2 (
    .S(or_2_out), .clk(or_4_out), .R(or_1_out), .Q(s_r_ff_2_q));  // open: Qn, preset, reset, en
  S_R_Flip_Flop #(.trigger("high")) s_r_ff_3 (
    .S(or_2_out), .clk(or_5_out), .R(or_1_out), .Q(s_r_ff_3_q));  // open: Qn, preset, reset, en
  S_R_Flip_Flop #(.trigger("high")) s_r_ff_4 (
    .S(or_2_out), .clk(or_6_out), .R(or_1_out), .Q(s_r_ff_4_q));  // open: Qn, preset, reset, en
  and and_1 (and_1_out, Zavreno, s_r_ff_1_q, s_r_ff_2_q, comparator_1_eq, comparator_2_eq, OK, comparator_3_eq, comparator_4_eq, s_r_ff_3_q, s_r_ff_4_q, Limit);
  Multiplexer #(.width(3), .enable("false")) multiplexer_1 (
    .in0(3'b000), .in1(3'b101), .out(_1__Cifra), .sel(s_r_ff_1_q));
  Multiplexer #(.width(3), .enable("false")) multiplexer_2 (
    .in0(3'b000), .in1(3'b101), .out(_2__Cifra), .sel(s_r_ff_2_q));
  Multiplexer #(.width(3), .enable("false")) multiplexer_3 (
    .in0(3'b000), .in1(3'b101), .out(_3__Cifra), .sel(s_r_ff_3_q));
  Multiplexer #(.width(3), .enable("false")) multiplexer_4 (
    .in0(3'b000), .in1(3'b101), .out(_4__Cifra), .sel(s_r_ff_4_q));
  T_Flip_Flop t_ff_1 (.clk(and_1_out), .T(and_1_out), .Q(\Odemknuto_Zamčeno ));  // open: Qn, preset, reset, en
  Counter #(.width(2), .max('h3), .ongoal("stay")) counter_2 (
    .Q(counter_2_q), .carry(counter_2_carry), .clk(and_2_out), .clr(or_7_out));  // open: load, D, count
  and and_2 (and_2_out, Zavreno, OK, s_r_ff_1_q, s_r_ff_2_q, s_r_ff_3_q, s_r_ff_4_q);
  or or_7 (or_7_out, Force_reset, \Odemknuto_Zamčeno );
  Multiplexer #(.width(3), .enable("false")) multiplexer_5 (
    .in0(3'b000), .in1(3'b111), .out(out_17), .sel(\Odemknuto_Zamčeno ));
  Subtractor #(.width(2)) subtractor_1 (.a(2'b11), .b(counter_2_q), .out(out_15[1:0]));  // open: bin, bout
  not not_1 (Limit, counter_2_carry);

  assign _1__Cifra_2 = {_1__Cifra[1], _1__Cifra[2:1]};
  assign _1__Cifra_3 = _1__Cifra;
  assign _2__Cifra_2 = {_2__Cifra[1], _2__Cifra[2:1]};
  assign _2__Cifra_3 = _2__Cifra;
  assign _3__Cifra_2 = {_3__Cifra[1], _3__Cifra[2:1]};
  assign _3__Cifra_3 = _3__Cifra;
  assign _4__Cifra_2 = {_4__Cifra[1], _4__Cifra[2:1]};
  assign _4__Cifra_3 = _4__Cifra;
  assign out_15[3:2] = 2'b00;
  assign out_18 = out_17;
  assign out_19 = out_17;
endmodule

module _4bitmemory (
  input  [3:0] Input,
  input  in_2,
  input  in_3,
  input  RESET,
  output [3:0] out_5
);

  wire and_1_out, and_2_out, and_3_out, and_4_out, and_5_out, or_1_out, or_2_out, or_3_out, or_4_out;

  and and_1 (and_1_out, in_2, in_3);
  and and_2 (and_2_out, Input[0], and_1_out);
  and and_3 (and_3_out, Input[1], and_1_out);
  and and_4 (and_4_out, Input[2], and_1_out);
  and and_5 (and_5_out, Input[3], and_1_out);
  or or_1 (or_1_out, RESET, and_1_out);
  or or_2 (or_2_out, RESET, and_1_out);
  or or_3 (or_3_out, RESET, and_1_out);
  or or_4 (or_4_out, RESET, and_1_out);
  D_Flip_Flop d_ff_1 (.clk(or_1_out), .D(and_2_out), .Q(out_5[0]));  // open: Qn, preset, en, reset
  D_Flip_Flop d_ff_2 (.clk(or_2_out), .D(and_3_out), .Q(out_5[1]));  // open: Qn, preset, en, reset
  D_Flip_Flop d_ff_3 (.clk(or_3_out), .D(and_4_out), .Q(out_5[2]));  // open: Qn, preset, en, reset
  D_Flip_Flop d_ff_4 (.clk(or_4_out), .D(and_5_out), .Q(out_5[3]));  // open: Qn, preset, en, reset
endmodule

module MatrixAuta (
  input  in_1,
  input  in_2,
  output [7:0] out_3,
  output [7:0] out_4,
  output [7:0] out_5,
  output [7:0] out_6,
  output [7:0] out_7,
  output [7:0] out_8,
  output [7:0] out_9,
  output [7:0] out_10,
  output [7:0] out_11,
  output [7:0] out_12,
  output [7:0] out_13,
  output [7:0] out_14,
  output [7:0] out_15,
  output [7:0] out_16,
  output [7:0] out_17,
  output [7:0] out_18,
  output [7:0] out_19,
  output [7:0] out_20,
  output [7:0] out_21,
  output [7:0] out_22,
  output [7:0] out_23,
  output [7:0] out_24,
  output [7:0] out_25,
  output [7:0] out_26,
  output [7:0] out_27,
  output [7:0] out_28,
  output [7:0] out_29,
  output [7:0] out_30
);

  wire and_1_out, and_2_out, and_3_out, clock_1_out, counter_1_carry, counter_2_carry, or_1_out, random_1_out;
  wire [3:0] counter_1_q;
  wire [7:0] multiplexer_1_out, multiplexer_2_out, multiplexer_3_out, shift_register_2_out;

  Clock clock_1 (.out(clock_1_out));
  Random #(.width(1)) random_1 (.clk(and_1_out), .out(random_1_out));  // open: next, clr
  Counter #(.width(4), .max('hf), .ongoal("stay")) counter_1 (
    .Q(counter_1_q), .carry(counter_1_carry), .clk(clock_1_out), .clr(and_1_out));  // open: load, D, count
  and and_1 (and_1_out, in_1, in_2);
  Multiplexer #(.select(4), .width(8), .enable("false")) multiplexer_1 (
    .in0(8'h1e), .in1(8'h27), .in2(8'h3f), .in3(8'h6), .in4(8'h3e), .in5(8'h3e), .in6(8'h3e), .in7(8'h3e),
    .in8(8'h3f), .in9(8'h3f), .in10(8'h3e), .in11({8{1'b0}}), .in12({8{1'b0}}), .in13({8{1'b0}}),
    .in14({8{1'b0}}), .in15({8{1'b0}}), .out(multiplexer_1_out), .sel(counter_1_q));
  Multiplexer #(.select(4), .width(8), .enable("false")) multiplexer_2 (
    .in0(8'h6), .in1(8'h7), .in2(8'h7), .in3(8'he), .in4(8'h16), .in5(8'h16), .in6(8'h16), .in7(8'hf),
    .in8(8'h7), .in9(8'he), .in10(8'h2), .in11({8{1'b0}}), .in12({8{1'b0}}), .in13({8{1'b0}}),
    .in14({8{1'b0}}), .in15({8{1'b0}}), .out(multiplexer_2_out), .sel(counter_1_q));
  Multiplexer #(.width(8), .enable("false")) multiplexer_3 (
    .in0(multiplexer_1_out), .in1(multiplexer_2_out), .out(multiplexer_3_out), .sel(random_1_out));
  Shift_Register #(.width(8), .length(13)) shift_register_1 (
    .in(multiplexer_3_out), .clk(clock_1_out), .q0(out_3), .q1(out_6), .q2(out_9), .q3(out_11), .q4(out_13),
    .q5(out_15), .q6(out_17), .q7(out_19), .q8(out_21), .q9(out_23), .q10(out_25), .q11(out_27), .q12(out_29));  // open: shift, out, load, clr, d0, d1, d2, d3, d4, d5, d6, d7, d8, d9, d10, d11, d12
  Counter #(.width(4), .max('hc), .ongoal("stay")) counter_2 (
    .carry(counter_2_carry), .clk(clock_1_out), .clr(and_1_out));  // open: load, D, count, Q
  and and_2 (and_2_out, ~counter_2_carry, clock_1_out);  // AND_Gate
  and and_3 (and_3_out, clock_1_out, counter_1_carry);
  Shift_Register #(.width(8), .length(13)) shift_register_2 (
    .in(multiplexer_3_out), .clk(or_1_out), .out(shift_register_2_out));  // open: shift, load, clr, d0, q0, d1, q1, d2, q2, d3, q3, d4, q4, d5, q5, d6, q6, d7, q7, d8, q8, d9, q9, d10, q10, d11, q11, d12, q12
  or or_1 (or_1_out, and_2_out, and_3_out);
  Shift_Register #(.width(8), .length(13)) shift_register_3 (
    .in(shift_register_2_out), .clk(clock_1_out), .q0(out_4), .q1(out_7), .q2(out_10), .q3(out_12),
    .q4(out_14), .q5(out_16), .q6(out_18), .q7(out_20), .q8(out_22), .q9(out_24), .q10(out_26), .q11(out_28),
    .q12(out_30));  // open: shift, out, load, clr, d0, d1, d2, d3, d4, d5, d6, d7, d8, d9, d10, d11, d12

  assign out_5 = {8{1'b1}};
  assign out_8 = {8{1'b1}};

  // Other names for the same wires on the sheet: _1[7:0] = out_3; _2[7:0] = out_6; _3[7:0] = out_9; _4[7:0] = out_11;
  //   _5[7:0] = out_13; _6[7:0] = out_15; _7[7:0] = out_17; _8[7:0] = out_19; _9[7:0] = out_21; _10[7:0] = out_23;
  //   _11[7:0] = out_25; _12[7:0] = out_27; _13[7:0] = out_29; _14[7:0] = out_4; _15[7:0] = out_7; _16[7:0] = out_10;
  //   _17[7:0] = out_12; _18[7:0] = out_14; _19[7:0] = out_16; _20[7:0] = out_18; _21[7:0] = out_20;
  //   _22[7:0] = out_22; _23[7:0] = out_24; _24[7:0] = out_26; _25[7:0] = out_28; _26[7:0] = out_30
endmodule

module CabelManagment (
  input  [7:0] in_1,
  input  [7:0] in_2,
  input  [7:0] in_3,
  input  [7:0] in_4,
  input  [7:0] in_5,
  input  [7:0] in_6,
  input  [7:0] in_7,
  input  [7:0] in_8,
  output [7:0] out_9,
  output [7:0] out_10,
  output [7:0] out_11,
  output [7:0] out_12,
  output [7:0] out_13,
  output [7:0] out_14,
  output [7:0] out_15,
  output [7:0] out_16
);


  assign out_9 = in_1;
  assign out_10 = in_2;
  assign out_11 = in_3;
  assign out_12 = in_4;
  assign out_13 = in_5;
  assign out_14 = in_6;
  assign out_15 = in_7;
  assign out_16 = in_8;
endmodule

module rendering (
  input  [7:0] in_1,
  input  [2:0] in_2,
  output [7:0] out_3
);

  Multiplexer #(.select(3), .width(8), .enable("false")) multiplexer_1 (
    .in0(in_1), .in1({in_1[6:0], 1'b0}), .in2({in_1[5:0], 2'b00}), .in3({in_1[4:0], 3'b000}),
    .in4({in_1[3:0], 4'b0000}), .in5({in_1[2:0], {5{1'b0}}}), .in6({in_1[1:0], {6{1'b0}}}), .in7({8{1'b0}}),
    .out(out_3), .sel(in_2));
endmodule

module renderingright (
  input  [7:0] in_1,
  input  [2:0] in_2,
  output [7:0] out_3
);

  Multiplexer #(.select(3), .width(8), .enable("false")) multiplexer_1 (
    .in0(in_1), .in1({1'b0, in_1[7:1]}), .in2({2'b00, in_1[7:2]}), .in3({3'b000, in_1[7:3]}),
    .in4({4'b0000, in_1[7:4]}), .in5({{5{1'b0}}, in_1[7:5]}), .in6({{6{1'b0}}, in_1[7:6]}), .in7({8{1'b0}}),
    .out(out_3), .sel(in_2));
endmodule
